# Fritzing sketch breadboard-prototype-two-rfids (saved by Fritzing 0.9.3b)
breadboards: 2

parts:
  U1 = NodeMCU V1.0
  Bauteil1 = RFID-RC522-v3
  Bauteil2 = RFID-RC522-v3
  IC1 = L293D [package=THT]
  M1 = DC Motor
  M2 = DC Motor

nets:
  N1: U1.D0, IC1.In_4
  N2: U1.D1, Bauteil1.RST, Bauteil2.RST
  N3: U1.D2, Bauteil1.SDA
  N4: U1.D3, IC1.Enable_1
  N5: U1.D4, IC1.Enable_2
  N6: U1.D5, Bauteil1.SCK, Bauteil2.SCK
  N7: U1.D6, Bauteil1.MISO, Bauteil2.MISO
  N8: U1.D7, Bauteil1.MOSI, Bauteil2.MOSI
  N9: U1.D8, IC1.In_2
  N10: U1.RX, IC1.In_3
  N11: U1.SD3, IC1.In_1
  N12: IC1.Out_1_(_Controlled_by_Enable_1_), M1.pin_2
  N13: IC1.Out_2_(_Controlled_by_Enable_1_), M1.pin_1
  N14: IC1.Out_3_(_Controlled_by_Enable_2_), M2.pin_2
  N15: IC1.Out_4_(_Controlled_by_Enable_2_), M2.pin_1

custom parts:
  NodeMCU V1.0: ESP8266 based NodeMCU
  RFID-RC522-v3: A simple China made RFID-RC522 Reader (6x4 cm); do check the pin labels, as this is a MFRC522 based clone.
