# Fritzing sketch esp32cam+led+button+servo+flash (saved by Fritzing 0.9.9b)
circuit board: 3.52777cm x 6.13807cm
circuit board: 9.74944cm x 4.27979cm
circuit board: 6.43454cm x 4.16036cm
breadboards: 1

parts:
  IC1 = L293D [package=THT]
  M2 = DC Motor
  M3 = DC Motor
  LED8 = smd LED [color="Red (633nm)" package="0805 [SMD]"]
  LED10 = smd LED [color="Red (633nm)" package="0805 [SMD]"]
  LED11 = smd LED [color="Red (633nm)" package="0805 [SMD]"]
  Mod1 = ESP32 - CAM
  VCC1 = Battery
  LED12 = smd LED [color="Red (633nm)" package="0805 [SMD]"]
  S4 = Pushbutton [package="[THT]"]
  M4 = DC Motor
  M5 = DC Motor
  VCC2 = Battery
  S5 = Pushbutton [package="[THT]"]
  LED13 = smd LED [color="Red (633nm)" package="0805 [SMD]"]
  LED14 = smd LED [color="Red (633nm)" package="0805 [SMD]"]
  LED15 = smd LED [color="Red (633nm)" package="0805 [SMD]"]
  LED16 = smd LED [color="Red (633nm)" package="0805 [SMD]"]
  Mod2 = ESP32 - CAM
  IC2 = L293D [package=THT]
  IC3 = L293D [package=THT]
  M6 = DC Motor
  M7 = DC Motor
  Mod3 = ESP32 - CAM
  VCC3 = Battery
  S6 = Pushbutton [package="[THT]"]
  LED17 = smd LED [color="Red (633nm)" package="0805 [SMD]"]
  LED18 = smd LED [color="Red (633nm)" package="0805 [SMD]"]
  LED19 = smd LED [color="Red (633nm)" package="0805 [SMD]"]
  LED20 = smd LED [color="Red (633nm)" package="0805 [SMD]"]

nets:
  N1: IC1.Enable_1, IC1.Enable_2, Mod1.IO4
  N2: IC1.In_1, Mod1.IO2
  N3: IC1.Out_1_(_Controlled_by_Enable_1_), M2.pin_2
  N4: IC1.0V, LED10.cathode, Mod1.GND, Mod1.IO12, VCC1.-, LED12.cathode, S4.Pin_1, S4.Pin_2
  N5: IC1.Out_2_(_Controlled_by_Enable_1_), M2.pin_1
  N6: IC1.In_2, Mod1.IO14
  N7: IC1.+Vmotor, IC1.+V, Mod1.5V, VCC1.+
  N8: IC1.In_3, Mod1.IO15
  N9: IC1.Out_3_(_Controlled_by_Enable_2_), M3.pin_2
  N10: IC1.Out_4_(_Controlled_by_Enable_2_), M3.pin_1
  N11: IC1.In_4, Mod1.IO13
  N12: LED8.cathode, LED11.cathode
  N13: LED8.anode, Mod1.IO16
  N14: LED10.anode, Mod1.VOR
  N15: LED11.anode, Mod1.VOT
  N16: Mod1.IO0, LED12.anode
  N17: M4.pin_1, IC2.Out_4_(_Controlled_by_Enable_2_)
  N18: M4.pin_2, IC2.Out_3_(_Controlled_by_Enable_2_)
  N19: M5.pin_1, IC2.Out_2_(_Controlled_by_Enable_1_)
  N20: M5.pin_2, IC2.Out_1_(_Controlled_by_Enable_1_)
  N21: VCC2.-, Mod2.5V, IC2.+Vmotor
  N22: S5.Pin_1, S5.Pin_2, Mod2.GND, Mod2.IO4, IC2.0V
  N23: LED13.cathode, LED14.cathode, LED15.cathode
  N24: LED13.anode, Mod2.IO2
  N25: LED14.anode, Mod2.IO13
  N26: LED15.anode, Mod2.IO15
  N27: LED16.anode, Mod2.IO14
  N28: Mod2.IO12, IC2.Enable_1, IC2.Enable_2
  N29: Mod2.VOT, IC2.In_4
  N30: Mod2.VOR, IC2.In_3
  N31: Mod2.VCC, IC2.+V
  N32: Mod2.IO0, IC2.In_2
  N33: Mod2.IO16, IC2.In_1
  N34: IC3.Enable_1, IC3.Enable_2, Mod3.IO4
  N35: IC3.Out_1_(_Controlled_by_Enable_1_), M7.pin_2
  N36: IC3.0V, Mod3.GND, VCC3.-, S6.Pin_1, S6.Pin_2, LED17.cathode, LED18.cathode
  N37: IC3.Out_2_(_Controlled_by_Enable_1_), M7.pin_1
  N38: IC3.In_2, Mod3.IO14
  N39: IC3.+Vmotor, IC3.+V, Mod3.5V, VCC3.+
  N40: IC3.In_3, Mod3.IO15
  N41: IC3.Out_3_(_Controlled_by_Enable_2_), M6.pin_2
  N42: IC3.Out_4_(_Controlled_by_Enable_2_), M6.pin_1
  N43: IC3.In_4, Mod3.IO13
  N44: Mod3.IO12, S6.Pin_3
  N45: Mod3.VOT, LED17.anode
  N46: Mod3.VOR, LED20.anode
  N47: Mod3.IO0, LED19.anode
  N48: Mod3.IO16, LED18.anode
  N49: LED19.cathode, LED20.cathode

custom parts:
  ESP32 - CAM: The ESP32-CAM has a very competitive small-size camera module that can operate independently as a minimum system with a footprint of only 27*40.5*4.5mm and a deep sleep current of up to 6mA.
