# Fritzing sketch nodemcu_two_rfidrc522 (saved by Fritzing 0.9.4)
circuit board: 8.46667cm x 5.64444cm
breadboards: 1

parts:
  U1 = NodeMCU V1.0
  Part1 = RFID-RC522-v3
  Part2 = RFID-RC522-v3

nets:
  N1: U1.D1, Part1.RST, Part2.RST
  N2: U1.D2, Part2.SDA
  N3: U1.D4, Part1.SDA
  3.3V: U1.3V3, Part1.3.3V, Part2.3.3V
  GND: U1.GND, Part1.GND, Part2.GND
  N4: U1.D5, Part1.SCK, Part2.SCK
  N5: U1.D6, Part1.MISO, Part2.MISO
  N6: U1.D7, Part1.MOSI, Part2.MOSI

custom parts:
  NodeMCU V1.0: ESP8266 based NodeMCU
  RFID-RC522-v3: A simple China made RFID-RC522 Reader (6x4 cm); do check the pin labels, as this is a MFRC522 based clone.
