# Fritzing sketch platine (saved by Fritzing 0.9.3b)
circuit board: 4.16463cm x 4.90649cm
breadboards: 1
perfboards: 1

parts:
  Raspberry_Pi_1 = Raspberry Pi 3 [part_number=RPI-3-V1.2]
  BAT1 = Battery Holders [package=battery-aa]
  M1 = DC Motor
  M2 = DC Motor
  J3 = female pin header, 6 pins [form="♀ (female)"]
  IC1 = L293D [package=THT]
  J4 = screw terminal, 2 pins
  J1 = Screw terminal - 2 pins [package=THT]
  J2 = Screw terminal - 2 pins [package=THT]

nets:
  N1: Raspberry_Pi_1.GPIO17, J3.pin5, IC1.In_4
  N2: Raspberry_Pi_1.GPIO27, J3.pin6, IC1.In_3
  N3: Raspberry_Pi_1.GPIO24, J3.pin1, IC1.In_2
  N4: Raspberry_Pi_1.GPIO23, J3.pin2, IC1.In_1
  N5: Raspberry_Pi_1.GND, BAT1.+, J3.pin3, IC1.0V, J4.pin2
  N6: Raspberry_Pi_1.5V, J3.pin4, IC1.+V
  N7: BAT1.-, IC1.+Vmotor, J4.pin1
  N8: M1.pin_1, IC1.Out_1_(_Controlled_by_Enable_1_), J2.pin1
  N9: M1.pin_2, IC1.Out_2_(_Controlled_by_Enable_1_), J2.pin2
  N10: M2.pin_1, J1.pin2
  N11: M2.pin_2, J1.pin1
