# Fritzing sketch prototype_1 (saved by Fritzing 0.9.3b)
breadboards: 1

parts:
  Raspberry_Pi_1 = Raspberry Pi 3 [part_number=RPI-3-V1.2]
  M1 = DC Motor
  M2 = DC Motor
  IC1 = L293D [package=THT]
  BAT1 = Battery Holders [package=battery-aa]
  BAT2 = Battery Holders [package=battery-aa]
  BAT3 = Battery Holders [package=battery-aa]
  BAT4 = Battery Holders [package=battery-aa]
  BAT5 = Battery Holders [package=battery-aa]
  BAT6 = Battery Holders [package=battery-aa]

nets:
  N1: Raspberry_Pi_1.GPIO17, Raspberry_Pi_1.GPIO18, IC1.In_4
  N2: Raspberry_Pi_1.GPIO27, IC1.In_3
  N3: Raspberry_Pi_1.GPIO24, IC1.In_1
  N4: Raspberry_Pi_1.GPIO23, IC1.In_2
  N5: Raspberry_Pi_1.GND, IC1.0V, BAT1.+
  N6: Raspberry_Pi_1.5V, IC1.+V
  N7: M1.pin_1, IC1.Out_3_(_Controlled_by_Enable_2_)
  N8: M1.pin_2, IC1.Out_4_(_Controlled_by_Enable_2_)
  N9: M2.pin_1, IC1.Out_2_(_Controlled_by_Enable_1_)
  N10: M2.pin_2, IC1.Out_1_(_Controlled_by_Enable_1_)
  N11: BAT1.-, BAT4.+
  N12: BAT2.-, BAT6.+
  N13: BAT2.+, BAT4.-
  N14: BAT3.-, BAT5.+
  N15: BAT3.+, BAT6.-
