# Fritzing sketch bot_board2 (saved by Fritzing 0.9.10b)
circuit board: 6cm x 4.5cm
breadboards: 1

parts:
  L293D = L293D [package=THT]
  Part1 = FTDI Basic Programmer  # not connected
  Part2 = FTDI Basic Programmer  # not connected
  ESP32_-_Back1 = ESP32 - CAM
  M1 = RioRand LM2596
  Motor1 = gear-motor
  Motor2 = gear-motor
  HeaderESP1 = female pin header, 8 pins [form="♀ (female)"]
  HeaderESP2 = female pin header, 8 pins [form="♀ (female)"]
  HeaderMotor1 = male pin header, 2 pins [form="♂ (male)"]
  HeaderMotor2 = male pin header, 2 pins [form="♂ (male)"]
  HeaderPower = double row male pin header, 2 pins [form="♂ (male)"]

nets:
  N1: L293D.Enable_1, L293D.Enable_2, ESP32_-_Back1.GPIO15, HeaderESP1.pin4
  N2: L293D.In_1, ESP32_-_Back1.GPIO14, HeaderESP1.pin3
  N3: L293D.Out_1_(_Controlled_by_Enable_1_), Motor1.pin_2, HeaderMotor1.pin1
  N4: L293D.0V, ESP32_-_Back1.GND#12, M1.Pin_4, HeaderESP2.pin5, HeaderPower.pin2
  N5: L293D.Out_2_(_Controlled_by_Enable_1_), Motor1.pin_1, HeaderMotor1.pin2
  N6: L293D.In_2, ESP32_-_Back1.GPIO2, HeaderESP1.pin2
  N7: L293D.+Vmotor, L293D.+V, ESP32_-_Back1.5V, M1.Pin_3, HeaderESP1.pin8, HeaderPower.pin1
  N8: L293D.In_3, ESP32_-_Back1.GPIO13, HeaderESP1.pin5
  N9: L293D.Out_3_(_Controlled_by_Enable_2_), Motor2.pin_1, HeaderMotor2.pin1
  N10: L293D.Out_4_(_Controlled_by_Enable_2_), Motor2.pin_2, HeaderMotor2.pin2
  N11: L293D.In_4, ESP32_-_Back1.GPIO12, HeaderESP1.pin6
  N12: ESP32_-_Back1.GPIO4, HeaderESP1.pin1
  N13: ESP32_-_Back1.GND#7, HeaderESP1.pin7
  N14: ESP32_-_Back1.3.3V, HeaderESP2.pin8
  N15: ESP32_-_Back1.GPIO16, HeaderESP2.pin7
  N16: ESP32_-_Back1.GPIO0, HeaderESP2.pin6
  N17: ESP32_-_Back1.3.3V_/_5V_/_P_OUT, HeaderESP2.pin4
  N18: ESP32_-_Back1.GPIO3_/_RX, HeaderESP2.pin3
  N19: ESP32_-_Back1.GPIO1_/_TX, HeaderESP2.pin2
  N20: ESP32_-_Back1.GND#16, HeaderESP2.pin1

custom parts:
  ESP32 - CAM: The ESP32-CAM has a very competitive small-size camera module that can operate independently as a minimum system with a footprint of only 27*40.5*4.5mm and a deep sleep current of up to 6mA.
